# Fritzing sketch tutorial-circuit (saved by Fritzing 0.9.3b)
breadboards: 1

parts:
  U2 = attiny85 [package=dip]
  LED1 = LED - 5mm [color="Green (555nm)" package="5 mm [THT]"]
  R1 = Resistor [tolerance=±5% resistance=220 package=THT]
  J2 = female pin header, 1 pin [form="♀ (female)"]
  J1 = single row smd female pin header, 2 pins [form="♀ (female)"]
  J3 = female pin header, 1 pin [form="♀ (female)"]

nets:
  GND: U2.Pin_4, LED1.cathode, J2.pin1
  N1: U2.Pin_5, J3.pin1
  N2: U2.Pin_6, R1.Pin_0
  N3: U2.Pin_7, J1.pin2
  N4: U2.Pin_8, J1.pin1
  N5: LED1.anode, R1.Pin_1

notes:
  GND
  SDA
  SCL
  +5V
